// Logisim project alu.circ as structural Verilog: 3 circuits, main circuit alu
module alu (
  input  [31:0] A,
  input  [31:0] B,
  input  [3:0] ALUSel,
  output [31:0] Result
);

  wire comparator_1_lt;
  wire [31:0] add0, and7, mul8, mulh9, mulhu11, or6, sll1, slt2, sra13, srl5, sub12, xor4;

  Adder #(.width(32)) adder_1 (.a(A), .b(B), .out(add0));  // open: cin, cout
  Shifter #(.width(32)) shifter_1 (.in(A), .\dist (B[4:0]), .out(sll1));
  Comparator #(.width(32)) comparator_1 (.a(A), .b(B), .lt(comparator_1_lt));  // open: gt, eq
  assign xor4 = A ^ B;  // XOR_Gate xor_1, 32 bits wide
  Shifter #(.shift("lr"), .width(32)) shifter_2 (.in(A), .\dist (B[4:0]), .out(srl5));
  assign or6 = A | B;  // OR_Gate or_1, 32 bits wide
  assign and7 = A & B;  // AND_Gate and_1, 32 bits wide
  Multiplier #(.mode("twosComplement"), .width(32)) multiplier_1 (.a(A), .b(B), .out(mul8));  // open: cin, cout
  Subtractor #(.width(32)) subtractor_1 (.a(A), .b(B), .out(sub12));  // open: bin, bout
  Shifter #(.shift("ar"), .width(32)) shifter_3 (.in(A), .\dist (B[4:0]), .out(sra13));
  assign slt2 = {{31{1'b0}}, comparator_1_lt};  // Bit_Extender bit_extender_1
  mulh mulh_1 (.A(A), .B(B), .Result(mulh9));
  mulhu mulhu_1 (.A(A), .B(B), .Result(mulhu11));
  Multiplexer #(.enable("false"), .select(4), .width(32)) multiplexer_1 (
    .in0(add0), .in1(sll1), .in2(slt2), .in4(xor4), .in5(srl5), .in6(or6), .in7(and7), .in8(mul8),
    .in9(mulh9), .in11(mulhu11), .in12(sub12), .in13(sra13), .in15(B), .out(Result), .sel(ALUSel));  // open: in3, in10, in14

  // Other names for the same wires on the sheet: bsel15[31:0] = B; unused[31:0] = A

  // Notes on the sheet:
  //   INPUTS to your circuit
  //   DON'T CHANGE THE LOCATIONS OF THE INPUTS AND OUTPUTS!
  //   OUTPUT from your circuit
endmodule

module mulh (
  input  [31:0] A,
  input  [31:0] B,
  output [31:0] Result
);

  wire [31:0] multiplier_1_out;
  wire [63:0] bit_extender_1_out, bit_extender_2_out;

  assign bit_extender_1_out = {{32{A[31]}}, A};  // Bit_Extender bit_extender_1
  assign bit_extender_2_out = {{32{B[31]}}, B};  // Bit_Extender bit_extender_2
  Multiplier #(.mode("twosComplement"), .width(64)) multiplier_1 (
    .a(bit_extender_1_out), .b(bit_extender_2_out), .out({Result, multiplier_1_out}));  // open: cin, cout
endmodule

module mulhu (
  input  [31:0] A,
  input  [31:0] B,
  output [31:0] Result
);

  wire [31:0] multiplier_1_out;
  wire [63:0] bit_extender_1_out, bit_extender_2_out;

  assign bit_extender_1_out = {{32{1'b0}}, A};  // Bit_Extender bit_extender_1
  assign bit_extender_2_out = {{32{1'b0}}, B};  // Bit_Extender bit_extender_2
  Multiplier #(.width(64)) multiplier_1 (
    .a(bit_extender_1_out), .b(bit_extender_2_out), .out({Result, multiplier_1_out}));  // open: cin, cout
endmodule
