// Logisim project branch-comp.circ as structural Verilog: 1 circuit, main circuit branch_comp
module branch_comp (
  input  [31:0] rs1,
  input  [31:0] rs2,
  input  BrUn,
  output BrEq,
  output BrLt
);

  wire [0:0] multiplexer_1_out;
  wire [2:0] comparator_1_gt, comparator_2_gt;

  Comparator #(.width(32)) comparator_1 (
    .a(rs1), .b(rs2), .gt(comparator_1_gt[0]), .eq(comparator_1_gt[1]), .lt(comparator_1_gt[2]));
  Comparator #(.mode("unsigned"), .width(32)) comparator_2 (
    .a(rs1), .b(rs2), .gt(comparator_2_gt[0]), .eq(comparator_2_gt[1]), .lt(comparator_2_gt[2]));
  Multiplexer #(.enable("false"), .width(3)) multiplexer_1 (
    .in0(comparator_1_gt), .in1(comparator_2_gt), .out({BrLt, BrEq, multiplexer_1_out[0]}), .sel(BrUn));

  // Notes on the sheet:
  //   INPUTS to your circuit
  //   DON'T CHANGE THE LOCATIONS OF THE INPUTS AND OUTPUTS!
  //   OUTPUT from your circuit
endmodule
