// Logisim project control-logic.circ as structural Verilog: 1 circuit, main circuit control_logic
module control_logic (
  input  [31:0] inst,
  input  BrEq,
  input  BrLt,
  output PCSel,
  output RegWEn,
  output [2:0] ImmSel,
  output BrUn,
  output ASel,
  output BSel,
  output [3:0] ALUSel,
  output MemRW,
  output [1:0] WBSel,
  output CSRSel,
  output CSRWen
);

  wire and_2_out, B, decoder_1_out4, decoder_1_out28, I, J, multiplexer_5_out, not_1_out, not_2_out, O0, O5,
       O13, O25, or_5_out, or_6_out, R, U;
  wire [1:0] multiplexer_1_out;
  wire [3:0] multiplexer_3_out;
  wire [3:3] and_1_out;

  Decoder #(.enable("false"), .select(5)) decoder_1 (
    .out0(O0), .out4(decoder_1_out4), .out5(O5), .out8(MemRW), .out12(R), .out13(O13), .out24(B),
    .out25(O25), .out27(J), .out28(decoder_1_out28), .sel(inst[6:2]));  // open: out1, out2, out3, out6, out7, out9, out10, out11, out14, out15, out16, out17, out18, out19, out20, out21, out22, out23, out26, out29, out30, out31
  or or_1 (RegWEn, R, I, J, U);
  or or_2 (I, O0, decoder_1_out4, O25, decoder_1_out28);
  or or_3 (U, O5, O13);
  or or_4 (ASel, O5, J, B);
  Priority_Encoder priority_encoder_1 (
    .in0(I), .in1(MemRW), .in2(B), .in3(U), .in4(J), .out(ImmSel));  // open: in5, in6, in7, en_in, gs, en_out
  and and_1 (and_1_out[3], inst[25], R);
  Multiplexer #(.enable("false"), .width(2)) multiplexer_1 (
    .in0(2'b01), .in1(2'b00), .out(multiplexer_1_out), .sel(O0));
  Multiplexer #(.enable("false"), .width(2)) multiplexer_2 (
    .in0(multiplexer_1_out), .in1(2'b10), .out(WBSel), .sel(or_5_out));
  or or_5 (or_5_out, O25, J);
  Multiplexer #(.enable("false"), .width(4)) multiplexer_3 (
    .in0({and_1_out[3], inst[14:12]}), .in1(4'b1111), .out(multiplexer_3_out), .sel(O13));
  not not_1 (not_1_out, BrEq);
  Multiplexer #(.enable("false"), .width(4)) multiplexer_4 (
    .in0(multiplexer_3_out), .in1(4'b0000), .out(ALUSel), .sel(or_6_out));
  or or_6 (or_6_out, B, MemRW, O5, O25, O0, J);
  Multiplexer #(.enable("false"), .select(3)) multiplexer_5 (
    .in0(BrEq), .in1(not_1_out), .in4(BrLt), .in5(not_2_out), .in6(BrLt), .in7(not_2_out),
    .out(multiplexer_5_out), .sel(inst[14:12]));  // open: in2, in3
  not not_2 (not_2_out, BrLt);
  or or_7 (BSel, I, B, MemRW, U, J);
  and and_2 (and_2_out, B, multiplexer_5_out);
  or or_8 (PCSel, O25, J, O5, and_2_out);

  assign BrUn = inst[13];

  // Other names for the same wires on the sheet: funct3[2:0] = inst[14:12]; opcode[6:0] = inst[6:0];
  //   funct7[6:0] = inst[31:25]; S = MemRW

  // Notes on the sheet:
  //   INPUTS to your circuit
  //   DON'T CHANGE THE LOCATIONS OF THE INPUTS AND OUTPUTS!
  //   OUTPUT from your circuit
endmodule
