// Logisim project cpu.circ as structural Verilog: 1 circuit, main circuit cpu
module cpu (
  input  clk,
  input  [31:0] INSTRUCTION,
  input  [31:0] READ_DATA,
  output [31:0] WRITE_ADDRESS,
  output [31:0] PROGRAM_COUNTER,
  output [31:0] ra,
  output [31:0] sp,
  output [31:0] t0,
  output [31:0] t1,
  output [31:0] t2,
  output [31:0] s0,
  output [31:0] s1,
  output [31:0] a0,
  output [31:0] tohost,
  output [3:0] WRITE_ENABLE,
  output [31:0] WRITE_DATA
);

  wire ASel, BrEq, BrLt, BrUn, BSel, lps, MemRW, PCSel, RegWEn;
  wire [1:0] WBSel;
  wire [2:0] funct3, ImmSel;
  wire [3:0] ALUSel;
  wire [6:0] funct7;
  wire [24:0] ins;
  wire [31:0] adder_2_out, bit_extender_1_out, c_ins_q, Imm, multiplexer_1_out, multiplexer_3_out,
       multiplexer_4_out, multiplexer_5_out, pc, PC_ADD4, Read_Data_1, WB_Data;

  Adder #(.width(32)) adder_1 (.a(PROGRAM_COUNTER), .b(32'h4), .out(PC_ADD4));  // open: cin, cout
  Multiplexer #(.enable("false"), .width(32)) multiplexer_1 (
    .in0(PC_ADD4), .in1(WRITE_ADDRESS), .out(multiplexer_1_out), .sel(PCSel));
  Register #(.width(32)) u_PC (.D(multiplexer_1_out), .clk(clk), .Q(PROGRAM_COUNTER));  // open: en, clr
  Register #(.width(1)) register_1 (.D(PCSel), .clk(clk), .Q(lps));  // open: en, clr
  Register #(.width(32)) c_ins (.D(INSTRUCTION), .clk(clk), .Q(c_ins_q));  // open: en, clr
  imm_gen imm_gen_1 (.inst({funct7, ins[24:15], funct3, ins[11:0]}), .ImmSel(ImmSel), .imm(Imm));
  control_logic control_logic_1 (
    .PCSel(PCSel), .RegWEn(RegWEn), .ImmSel(ImmSel), .BrUn(BrUn), .ASel(ASel), .BSel(BSel), .ALUSel(ALUSel),
    .MemRW(MemRW), .WBSel(WBSel), .inst({funct7, ins[24:15], funct3, ins[11:0]}), .BrEq(BrEq), .BrLt(BrLt));  // open: CSRWen, CSRSel
  Register #(.width(32)) c_pc (.D(PROGRAM_COUNTER), .clk(clk), .Q(pc));  // open: en, clr
  Multiplexer #(.enable("false"), .width(32)) multiplexer_2 (
    .in0(c_ins_q), .in1(32'h13), .out({funct7, ins[24:15], funct3, ins[11:0]}), .sel(lps));
  branch_comp branch_comp_1 (.rs1(Read_Data_1), .rs2(WRITE_DATA), .BrUn(BrUn), .BrEq(BrEq), .BrLt(BrLt));
  assign bit_extender_1_out = {{27{1'b0}}, ins[19:15]};  // Bit_Extender bit_extender_1
  regfile regfile_1 (
    .rs1(ins[19:15]), .rs2(ins[24:20]), .rd(ins[11:7]), .Write_Data(WB_Data), .RegWEn(RegWEn), .clk(clk),
    .ra(ra), .sp(sp), .t0(t0), .t1(t1), .t2(t2), .s0(s0), .s1(s1), .a0(a0), .Read_Data_1(Read_Data_1),
    .Read_Data_2(WRITE_DATA));
  Multiplexer #(.enable("false"), .width(32)) multiplexer_3 (
    .in0(Read_Data_1), .in1(bit_extender_1_out), .out(multiplexer_3_out), .sel(funct3[2]));
  // csr csr_1: pin names not known; wires that end beside it: {funct7, ins[24:20]}, multiplexer_3_out, ins[1], clk, tohost
  Adder #(.width(32)) adder_2 (.a(pc), .b(32'h4), .out(adder_2_out));  // open: cin, cout
  assign WRITE_ENABLE = {{3{MemRW}}, MemRW};  // Bit_Extender bit_extender_2
  Multiplexer #(.enable("false"), .width(32)) multiplexer_4 (
    .in0(Read_Data_1), .in1(pc), .out(multiplexer_4_out), .sel(ASel));
  Multiplexer #(.enable("false"), .width(32)) multiplexer_5 (
    .in0(WRITE_DATA), .in1(Imm), .out(multiplexer_5_out), .sel(BSel));
  Multiplexer #(.enable("false"), .select(2), .width(32)) multiplexer_6 (
    .in0(READ_DATA), .in1(WRITE_ADDRESS), .in2(adder_2_out), .out(WB_Data), .sel(WBSel));  // open: in3
  alu alu_1 (.Result(WRITE_ADDRESS), .A(multiplexer_4_out), .B(multiplexer_5_out), .ALUSel(ALUSel));

  // Other names for the same wires on the sheet: ALU_Result[31:0] = WRITE_ADDRESS; opcode[6:0] = ins[6:0];
  //   rd[4:0] = ins[11:7]; ins (some bits) = {funct7, funct3}; rs1[4:0] = ins[19:15]; rs2[4:0] = ins[24:20];
  //   Read_Data_2[31:0] = WRITE_DATA

  // Notes on the sheet:
  //   Output to IMEM
  //   IMEM (do **NOT** move this)
  //   Inputs from IMEM
  //   It is OK to move the PC, RegFile, ALU, MEM, Branch Comp, Imm Gen, and Control Logic to wherever is most convenient for you when constructing your CPU, and to delete this text
  //   Inputs/Outputs for testing. Do **NOT** move these.
  //   Outputs To DMEM
  //   DMEM (do **NOT** move this)
  //   Inputs From DMEM
endmodule
