// Logisim project regfile.circ as structural Verilog: 1 circuit, main circuit regfile
// x0
module regfile (
  input  [4:0] rs1,
  input  [4:0] rs2,
  input  [4:0] rd,
  input  [31:0] Write_Data,
  input  RegWEn,
  input  clk,
  output [31:0] ra,
  output [31:0] sp,
  output [31:0] t0,
  output [31:0] t1,
  output [31:0] t2,
  output [31:0] s0,
  output [31:0] s1,
  output [31:0] a0,
  output [31:0] Read_Data_1,
  output [31:0] Read_Data_2
);

  wire W0, W1, W2, W3, W4, W5, W6, W7, W8, W9, W10, W11, W12, W13, W14, W15, W16, W17, W18, W19, W20, W21,
       W22, W23, W24, W25, W26, W27, W28, W29, W30, W31;
  wire [31:0] Q0, Q3, Q4, Q11, Q12, Q13, Q14, Q15, Q16, Q17, Q18, Q19, Q20, Q21, Q22, Q23, Q24, Q25, Q26,
       Q27, Q28, Q29, Q30, Q31, RR0, RR1, RR2, RR3, RR10, RR11, RR12, RR13;

  Register #(.width(32)) register_1 (.D(Write_Data), .en(W0), .clk(clk), .Q(Q0), .clr(1'b1));
  Register #(.width(32)) register_2 (.D(Write_Data), .en(W1), .clk(clk), .Q(ra));  // open: clr
  Register #(.width(32)) register_3 (.D(Write_Data), .en(W2), .clk(clk), .Q(sp));  // open: clr
  Register #(.width(32)) register_4 (.D(Write_Data), .en(W3), .clk(clk), .Q(Q3));  // open: clr
  Multiplexer #(.enable("false"), .select(3), .width(32)) multiplexer_1 (
    .in0(Q0), .in1(ra), .in2(sp), .in3(Q3), .in4(Q4), .in5(t0), .in6(t1), .in7(t2), .out(RR0), .sel(rs1[2:0]));
  Multiplexer #(.enable("false"), .select(2), .width(32)) multiplexer_2 (
    .in0(RR0), .in1(RR1), .in2(RR2), .in3(RR3), .out(Read_Data_1), .sel(rs1[4:3]));
  Register #(.width(32)) register_5 (.D(Write_Data), .en(W4), .clk(clk), .Q(Q4));  // open: clr
  Register #(.width(32)) register_6 (.D(Write_Data), .en(W5), .clk(clk), .Q(t0));  // open: clr
  Register #(.width(32)) register_7 (.D(Write_Data), .en(W6), .clk(clk), .Q(t1));  // open: clr
  Register #(.width(32)) register_8 (.D(Write_Data), .en(W7), .clk(clk), .Q(t2));  // open: clr
  Multiplexer #(.enable("false"), .select(3), .width(32)) multiplexer_3 (
    .in0(s0), .in1(s1), .in2(a0), .in3(Q11), .in4(Q12), .in5(Q13), .in6(Q14), .in7(Q15), .out(RR1),
    .sel(rs1[2:0]));
  Register #(.width(32)) register_9 (.D(Write_Data), .en(W8), .clk(clk), .Q(s0));  // open: clr
  Register #(.width(32)) register_10 (.D(Write_Data), .en(W9), .clk(clk), .Q(s1));  // open: clr
  Register #(.width(32)) register_11 (.D(Write_Data), .en(W10), .clk(clk), .Q(a0));  // open: clr
  Register #(.width(32)) register_12 (.D(Write_Data), .en(W11), .clk(clk), .Q(Q11));  // open: clr
  Multiplexer #(.enable("false"), .select(3), .width(32)) multiplexer_4 (
    .in0(Q16), .in1(Q17), .in2(Q18), .in3(Q19), .in4(Q20), .in5(Q21), .in6(Q22), .in7(Q23), .out(RR2),
    .sel(rs1[2:0]));
  Register #(.width(32)) register_13 (.D(Write_Data), .en(W12), .clk(clk), .Q(Q12));  // open: clr
  Register #(.width(32)) register_14 (.D(Write_Data), .en(W13), .clk(clk), .Q(Q13));  // open: clr
  Register #(.width(32)) register_15 (.D(Write_Data), .en(W14), .clk(clk), .Q(Q14));  // open: clr
  Register #(.width(32)) register_16 (.D(Write_Data), .en(W15), .clk(clk), .Q(Q15));  // open: clr
  Multiplexer #(.enable("false"), .select(3), .width(32)) multiplexer_5 (
    .in0(Q24), .in1(Q25), .in2(Q26), .in3(Q27), .in4(Q28), .in5(Q29), .in6(Q30), .in7(Q31), .out(RR3),
    .sel(rs1[2:0]));
  Register #(.width(32)) register_17 (.D(Write_Data), .en(W16), .clk(clk), .Q(Q16));  // open: clr
  Register #(.width(32)) register_18 (.D(Write_Data), .en(W17), .clk(clk), .Q(Q17));  // open: clr
  Register #(.width(32)) register_19 (.D(Write_Data), .en(W18), .clk(clk), .Q(Q18));  // open: clr
  Register #(.width(32)) register_20 (.D(Write_Data), .en(W19), .clk(clk), .Q(Q19));  // open: clr
  Register #(.width(32)) register_21 (.D(Write_Data), .en(W20), .clk(clk), .Q(Q20));  // open: clr
  Register #(.width(32)) register_22 (.D(Write_Data), .en(W21), .clk(clk), .Q(Q21));  // open: clr
  Register #(.width(32)) register_23 (.D(Write_Data), .en(W22), .clk(clk), .Q(Q23));  // open: clr
  Register #(.width(32)) register_24 (.D(Write_Data), .en(W23), .clk(clk), .Q(Q23));  // open: clr
  Multiplexer #(.enable("false"), .select(3), .width(32)) multiplexer_6 (
    .in0(Q0), .in1(ra), .in2(sp), .in3(Q3), .in4(Q4), .in5(t0), .in6(t1), .in7(t2), .out(RR10), .sel(rs2[2:0]));
  Multiplexer #(.enable("false"), .select(2), .width(32)) multiplexer_7 (
    .in0(RR10), .in1(RR11), .in2(RR12), .in3(RR13), .out(Read_Data_2), .sel(rs2[4:3]));
  Register #(.width(32)) register_25 (.D(Write_Data), .en(W24), .clk(clk), .Q(Q24));  // open: clr
  Register #(.width(32)) register_26 (.D(Write_Data), .en(W25), .clk(clk), .Q(Q25));  // open: clr
  Register #(.width(32)) register_27 (.D(Write_Data), .en(W26), .clk(clk), .Q(Q26));  // open: clr
  Register #(.width(32)) register_28 (.D(Write_Data), .en(W27), .clk(clk), .Q(Q27));  // open: clr
  Multiplexer #(.enable("false"), .select(3), .width(32)) multiplexer_8 (
    .in0(s0), .in1(s1), .in2(a0), .in3(Q11), .in4(Q12), .in5(Q13), .in6(Q14), .in7(Q15), .out(RR11),
    .sel(rs2[2:0]));
  Register #(.width(32)) register_29 (.D(Write_Data), .en(W28), .clk(clk), .Q(Q28));  // open: clr
  Register #(.width(32)) register_30 (.D(Write_Data), .en(W29), .clk(clk), .Q(Q29));  // open: clr
  Register #(.width(32)) register_31 (.D(Write_Data), .en(W30), .clk(clk), .Q(Q30));  // open: clr
  Register #(.width(32)) register_32 (.D(Write_Data), .en(W31), .clk(clk), .Q(Q31));  // open: clr
  Multiplexer #(.enable("false"), .select(3), .width(32)) multiplexer_9 (
    .in0(Q16), .in1(Q17), .in2(Q18), .in3(Q19), .in4(Q20), .in5(Q21), .in6(Q22), .in7(Q23), .out(RR12),
    .sel(rs2[2:0]));
  Multiplexer #(.enable("false"), .select(3), .width(32)) multiplexer_10 (
    .in0(Q24), .in1(Q25), .in2(Q26), .in3(Q27), .in4(Q28), .in5(Q29), .in6(Q30), .in7(Q31), .out(RR13),
    .sel(rs2[2:0]));
  Demultiplexer #(.enable("false"), .select(5)) demultiplexer_1 (
    .out0(W0), .out1(W1), .out2(W2), .out3(W3), .out4(W4), .out5(W5), .out6(W6), .out7(W7), .out8(W8),
    .out9(W9), .out10(W10), .out11(W11), .out12(W12), .out13(W13), .out14(W14), .out15(W15), .out16(W16),
    .out17(W17), .out18(W18), .out19(W19), .out20(W20), .out21(W21), .out22(W22), .out23(W23), .out24(W24),
    .out25(W25), .out26(W26), .out27(W27), .out28(W28), .out29(W29), .out30(W30), .out31(W31), .in(RegWEn),
    .sel(rd));

  // Other names for the same wires on the sheet: D0[31:0] = Write_Data; D1[31:0] = Write_Data; D2[31:0] = Write_Data;
  //   D3[31:0] = Write_Data; D4[31:0] = Write_Data; D5[31:0] = Write_Data; D6[31:0] = Write_Data;
  //   D7[31:0] = Write_Data; D8[31:0] = Write_Data; D9[31:0] = Write_Data; D10[31:0] = Write_Data;
  //   D11[31:0] = Write_Data; D12[31:0] = Write_Data; D13[31:0] = Write_Data; D14[31:0] = Write_Data;
  //   D15[31:0] = Write_Data; D16[31:0] = Write_Data; D17[31:0] = Write_Data; D18[31:0] = Write_Data;
  //   D19[31:0] = Write_Data; D20[31:0] = Write_Data; D21[31:0] = Write_Data; D22[31:0] = Write_Data;
  //   D23[31:0] = Write_Data; D24[31:0] = Write_Data; D25[31:0] = Write_Data; D26[31:0] = Write_Data;
  //   D27[31:0] = Write_Data; D28[31:0] = Write_Data; D29[31:0] = Write_Data; D30[31:0] = Write_Data;
  //   D31[31:0] = Write_Data; Q1[31:0] = ra; Q2[31:0] = sp; Q5[31:0] = t0; Q6[31:0] = t1; Q7[31:0] = t2;
  //   Q8[31:0] = s0; Q9[31:0] = s1; Q10[31:0] = a0; read_data1[31:0] = Read_Data_1; read_data2[31:0] = Read_Data_2;
  //   read_reg1[4:0] = rs1; sel1[2:0] = rs1[2:0]; sel2[1:0] = rs1[4:3]; read_reg2[4:0] = rs2; sel11[2:0] = rs2[2:0];
  //   sel12[1:0] = rs2[4:3]; write_en = RegWEn; write_reg[4:0] = rd

  // Notes on the sheet:
  //   INPUTS to your circuit
  //   DON'T CHANGE THE LOCATIONS OF THE INPUTS AND OUTPUTS!
  //   These are DEBUG/TEST outputs from your circuit.
  //   OUTPUTS from your circuit
endmodule
